# Fritzing sketch pi proj (saved by Fritzing 0.9.2b)
breadboards: 1

parts:
  Arduino_UNO = Arduino Uno (Rev3)
  Raspberry_Pi1 = Raspberry Pi B+
  R1 = Resistor [tolerance=±5% resistance=220 package=THT]
  R2 = Resistor [tolerance=±5% resistance=220 package=THT]
  LED1 = LED - 5mm [color="Red (633nm)" package="5 mm [THT]"]
  R3 = Resistor [tolerance=±5% resistance=220 package=THT]

nets:
  N1: Arduino_UNO.D12/MISO, LED1.anode
  N2: Arduino_UNO.GND, R3.Pin_0
  N3: Arduino_UNO.D6_PWM, R2.Pin_0
  N4: Arduino_UNO.D7, R1.Pin_0
  N5: Raspberry_Pi1.GPIO17, R2.Pin_1
  N6: Raspberry_Pi1.GPIO27, R1.Pin_1
  N7: LED1.cathode, R3.Pin_1

notes:
  GPIO 27 purple
  GPIO 17 yellow
